// Logisim project Intro_circuit.circ as structural Verilog: 1 circuit, main circuit main
module main (
  input  a,
  input  b,
  output s,
  output c
);

  wire and_1_out, and_2_out, not_1_out, not_2_out;

  not not_1 (not_1_out, a);
  not not_2 (not_2_out, b);
  and and_1 (and_1_out, b, not_1_out);
  and and_2 (and_2_out, not_2_out, a);
  and and_3 (c, b, a);
  or or_1 (s, and_1_out, and_2_out);

  // Notes on the sheet:
  //   s = !ab + a(!b)
  //   c = ab
endmodule
